# Fritzing sketch DS18B20-Holder-x6-phono (saved by Fritzing 1.0.4)
circuit board: 5.12528cm x 2.31255cm
breadboards: 1

parts:
  R1 = Resistor [tolerance=±20% power=0.5W resistance=4.7k package=THT]
  J2 = male pin header, 3 pins [form="♂ (male)"]
  J1 = screw terminal, 3 pins
  Part1 = TRRS 3.5mm Jack Breakout  # not connected
  Part2 = TRRS 3.5mm Jack Breakout  # not connected
  Part3 = TRRS 3.5mm Jack Breakout  # not connected
  Part4 = TRRS 3.5mm Jack Breakout  # not connected
  Part5 = TRRS 3.5mm Jack Breakout  # not connected
  Part6 = TRRS 3.5mm Jack Breakout  # not connected

nets:
  N1: R1.Pin_0, J1.pin2
  N2: R1.Pin_1, J2.pin3, J1.pin3
  N3: J2.pin1, J1.pin1

notes:
  ©Adam Howell
  p
  n
  +
  -
